# Fritzing sketch MCU (saved by Fritzing 0.9.3b)
breadboards: 1

parts:
  元件1 = Arduino Mega 2560 (Rev3)
  S1 = Pushbutton [package="[THT]"]
  J1 = Basic Servo
  SG1 = Buzzer 12mm [package=buzzer-12mm-ns]

nets:
  N1: 元件1.D21/SCL, 元件1.SCL, S1.Pin_3, S1.Pin_4
  N2: 元件1.GND, S1.Pin_2, SG1.1
  N3: 元件1.D2_PWM, SG1.2
  N4: 元件1.D3_PWM, J1.pulse
